# Fritzing sketch ledpong (saved by Fritzing 0.9.3b)
breadboards: 1

parts:
  Componente1 = Arduino Uno (Rev3)
  S1 = Pushbutton [package="[THT]"]
  R1 = Resistor [tolerance=±5% resistance=220 package=THT]
  LED2 = LED - 5mm [color="Green (560nm)" package="5 mm [THT]"]
  LED3 = LED - 5mm [color="Red (633nm)" package="5 mm [THT]"]
  R2 = Resistor [tolerance=±5% resistance=220 package=THT]
  S2 = Pushbutton [package="[THT]"]
  LED4 = LED - 5mm [color="Green (560nm)" package="5 mm [THT]"]
  R3 = Resistor [tolerance=±5% resistance=220 package=THT]
  LED5 = LED - 5mm [color="Green (560nm)" package="5 mm [THT]"]
  R4 = Resistor [tolerance=±5% resistance=220 package=THT]
  S3 = Pushbutton [package="[THT]"]
  R5 = Resistor [tolerance=±5% resistance=10k package=THT]
  R6 = Resistor [tolerance=±5% resistance=10k package=THT]
  R7 = Resistor [tolerance=±5% resistance=10k package=THT]
  R8 = Rotary Potentiometer (Small) [maximum_resistance=100kΩ package=THT]

nets:
  N1: Componente1.A0, R8.wiper
  N2: Componente1.D9_PWM, R1.Pin_1
  N3: Componente1.D10_PWM/SS, R4.Pin_1
  N4: Componente1.D11_PWM/MOSI, R3.Pin_1
  N5: Componente1.D12/MISO, R2.Pin_1
  N6: Componente1.GND, LED2.cathode, LED3.cathode, LED4.cathode, LED5.cathode, R6.Pin_1, R7.Pin_1, R8.leg1
  N7: Componente1.D2, S3.Pin_3, S3.Pin_4, R5.Pin_0
  N8: Componente1.D3_PWM, S2.Pin_3, S2.Pin_4, R6.Pin_0
  N9: Componente1.D4, S1.Pin_3, S1.Pin_4, R7.Pin_0
  N10: Componente1.5V, S1.Pin_1, S1.Pin_2, S2.Pin_1, S2.Pin_2, S3.Pin_1, S3.Pin_2, R8.leg2
  N11: R1.Pin_0, LED3.anode
  N12: LED2.anode, R2.Pin_0
  N13: LED4.anode, R3.Pin_0
  N14: LED5.anode, R4.Pin_0
