# Fritzing sketch smart_coffee_machine (saved by Fritzing 0.9.3b)
breadboards: 1

parts:
  Componente1 = Arduino Uno (Rev3)
  S1 = Pushbutton [package="[THT]"]
  R1 = Rotary Potentiometer (Small) [maximum_resistance=100kΩ package=THT]
  R2 = Resistor [tolerance=±5% resistance=220 package=THT]
  R3 = Resistor [tolerance=±5% resistance=220 package=THT]
  R4 = Resistor [tolerance=±5% resistance=220 package=THT]
  R5 = Resistor [tolerance=±5% resistance=10k package=THT]
  hc-sr1 = hc-sr04
  LED1 = LED - 5mm [color="Green (555nm)" package="5 mm [THT]"]
  LED2 = LED - 5mm [color="Green (555nm)" package="5 mm [THT]"]
  LED3 = LED - 5mm [color="Green (555nm)" package="5 mm [THT]"]
  PIR1 = PIR sensor

nets:
  N1: Componente1.A0, R1.wiper
  N2: Componente1.D8, R2.Pin_1
  N3: Componente1.D9_PWM, R3.Pin_1
  N4: Componente1.D1/TX, hc-sr1.Echo
  N5: Componente1.D2, hc-sr1.Trig
  N6: Componente1.D3_PWM, PIR1.SIG
  N7: Componente1.D4, S1.Pin_3, S1.Pin_4, R5.Pin_0
  N8: Componente1.D7, R4.Pin_1
  5V: Componente1.5V, S1.Pin_1, S1.Pin_2, R1.leg1, hc-sr1.VCC, PIR1.VDD
  GND: Componente1.GND, R1.leg2, R5.Pin_1, hc-sr1.GND, LED1.cathode, LED2.cathode, LED3.cathode, PIR1.GND
  N9: R2.Pin_0, LED2.anode
  N10: R3.Pin_0, LED3.anode
  N11: R4.Pin_0, LED1.anode
