# Fritzing sketch schema (saved by Fritzing 0.9.3b)
breadboards: 1

parts:
  Componente1 = Arduino Uno (Rev3)
  U1 = ESP8266 WiFi Module [part_number=ESP8266]
  LED1 = LED - 5mm [color="Green (555nm)" package="5 mm [THT]"]
  LED2 = LED - 5mm [color="Green (555nm)" package="5 mm [THT]"]
  LED3 = LED - 5mm [color="Red (633nm)" package="5 mm [THT]"]
  R1 = Resistor [tolerance=±5% resistance=220 package=THT]
  R2 = Resistor [tolerance=±5% resistance=220 package=THT]
  R3 = Resistor [tolerance=±5% resistance=220 package=THT]
  R4 = Rotary Potentiometer (Small) [maximum_resistance=100kΩ package=THT]
  Componente2 = Bluetooth HC-05 Macho
  hc-sr1 = hc-sr04
  J1 = Basic Servo

nets:
  N1: Componente1.D8, J1.pulse
  N2: Componente1.D12/MISO, hc-sr1.Trig
  N3: Componente1.D13/SCK, hc-sr1.Echo
  N4: Componente1.D1/TX, Componente2.TXD
  N5: Componente1.D2, Componente2.RXD
  N6: Componente1.D4, R1.Pin_1
  N7: Componente1.D5_PWM, R2.Pin_1
  N8: Componente1.D6_PWM, R3.Pin_1
  VCC: Componente1.5V, U1.VCC, R4.leg1, Componente2.VCC, hc-sr1.VCC, J1.vcc
  GND: Componente1.GND, U1.GND, LED1.cathode, LED2.cathode, LED3.cathode, R4.leg2, Componente2.GND, hc-sr1.GND, J1.gnd
  N9: U1.ADC_0, R4.wiper
  N10: LED1.anode, R1.Pin_0
  N11: LED2.anode, R2.Pin_0
  N12: LED3.anode, R3.Pin_0
